// Logisim project ALU.circ as structural Verilog: 5 circuits, main circuit decodeur
module decodeur (
  input  a1,
  input  a0,
  output s3,
  output s2,
  output s1,
  output s0
);

  wire not_1_out, not_2_out;

  not not_1 (not_1_out, a1);
  not not_2 (not_2_out, a0);
  and and_1 (s3, a1, a0);
  and and_2 (s2, a1, not_2_out);
  and and_3 (s1, not_1_out, a0);
  and and_4 (s0, not_1_out, not_2_out);
endmodule

module multiplexeur (
  input  e3,
  input  e2,
  input  e1,
  input  e0,
  input  a1,
  input  a0,
  output out_7
);

  wire and_1_out, and_2_out, and_3_out, and_4_out, decodeur_1_s0, decodeur_1_s1, decodeur_1_s2, decodeur_1_s3;

  decodeur decodeur_1 (
    .a1(a1), .a0(a0), .s3(decodeur_1_s3), .s2(decodeur_1_s2), .s1(decodeur_1_s1), .s0(decodeur_1_s0));
  and and_1 (and_1_out, e3, decodeur_1_s3);
  and and_2 (and_2_out, e2, decodeur_1_s2);
  and and_3 (and_3_out, e1, decodeur_1_s1);
  and and_4 (and_4_out, e0, decodeur_1_s0);
  or or_1 (out_7, and_1_out, and_2_out, and_3_out, and_4_out);
endmodule

module additionneur (
  input  a,
  input  b,
  input  cin,
  output s,
  output cout
);

  wire and_1_out, and_2_out, and_3_out;

  xor odd_parity_1 (s, a, b, cin);
  and and_1 (and_1_out, a, b);
  and and_2 (and_2_out, a, cin);
  and and_3 (and_3_out, b, cin);
  or or_1 (cout, and_1_out, and_2_out, and_3_out);
endmodule

module alu1bit (
  input  a,
  input  b,
  input  cin,
  input  s1,
  input  s0,
  output f,
  output cout
);

  wire additionneur_1_s, and_1_out, not_1_out, or_1_out;

  not not_1 (not_1_out, a);
  and and_1 (and_1_out, a, b);
  or or_1 (or_1_out, a, b);
  additionneur additionneur_1 (.a(a), .b(b), .cin(cin), .s(additionneur_1_s), .cout(cout));
  multiplexeur multiplexeur_1 (
    .e3(additionneur_1_s), .e2(or_1_out), .e1(and_1_out), .e0(not_1_out), .a1(s1), .a0(s0), .out_7(f));
endmodule

module alu4bits (
  input  [3:0] A,
  input  [3:0] B,
  input  s1,
  input  s0,
  output out_5,
  output out_6,
  output out_7,
  output out_8,
  output out_9
);

  wire alu1bit_1_cout, alu1bit_2_cout, alu1bit_3_cout;

  alu1bit alu1bit_1 (.a(A[0]), .b(B[0]), .s1(s1), .s0(s0), .f(out_5), .cout(alu1bit_1_cout));  // open: cin
  alu1bit alu1bit_2 (.a(A[1]), .b(B[1]), .cin(alu1bit_1_cout), .s1(s1), .s0(s0), .f(out_6), .cout(alu1bit_2_cout));
  alu1bit alu1bit_3 (.a(A[2]), .b(B[2]), .cin(alu1bit_2_cout), .s1(s1), .s0(s0), .f(out_7), .cout(alu1bit_3_cout));
  alu1bit alu1bit_4 (.a(A[3]), .b(B[3]), .cin(alu1bit_3_cout), .s1(s1), .s0(s0), .f(out_8), .cout(out_9));
endmodule
