// Logisim project Addition.circ as structural Verilog: 9 circuits, main circuit demi_additionneur
module demi_additionneur (
  input  a,
  input  b,
  output r,
  output s
);

  and and_1 (r, a, b);
  xor xor_1 (s, a, b);
endmodule

module additionneur_complet1 (
  input  a,
  input  b,
  input  rin,
  output rout,
  output s
);

  wire demi_additionneur_1_r, demi_additionneur_1_s, demi_additionneur_2_r;

  demi_additionneur demi_additionneur_1 (.a(a), .b(b), .r(demi_additionneur_1_r), .s(demi_additionneur_1_s));
  demi_additionneur demi_additionneur_2 (.a(demi_additionneur_1_s), .b(rin), .r(demi_additionneur_2_r), .s(s));
  or or_1 (rout, demi_additionneur_1_r, demi_additionneur_2_r);
endmodule

module additionneur_complet2 (
  input  a,
  input  b,
  input  rin,
  output rout,
  output s
);

  wire and_1_out, and_2_out, and_3_out, and_4_out, and_5_out, and_6_out, and_7_out, not_1_out, not_2_out,
       not_3_out;

  not not_1 (not_1_out, a);
  not not_2 (not_2_out, b);
  not not_3 (not_3_out, rin);
  and and_1 (and_1_out, b, rin);
  and and_2 (and_2_out, a, rin);
  and and_3 (and_3_out, a, b);
  and and_4 (and_4_out, not_1_out, not_2_out, rin);
  and and_5 (and_5_out, not_1_out, b, not_3_out);
  and and_6 (and_6_out, a, not_2_out, not_3_out);
  and and_7 (and_7_out, a, b, rin);
  or or_1 (rout, and_1_out, and_2_out, and_3_out);
  or or_2 (s, and_4_out, and_5_out, and_6_out, and_7_out);
endmodule

module additionneur4bits (
  input  [3:0] A,
  input  [3:0] B,
  input  r0,
  output r4,
  output [3:0] out_5
);

  wire additionneur_complet2_2_rout, additionneur_complet2_3_rout, additionneur_complet2_4_rout;

  additionneur_complet2 additionneur_complet2_1 (
    .a(A[3]), .b(B[3]), .rin(additionneur_complet2_2_rout), .rout(r4), .s(out_5[3]));
  additionneur_complet2 additionneur_complet2_2 (
    .a(A[2]), .b(B[2]), .rin(additionneur_complet2_3_rout), .rout(additionneur_complet2_2_rout), .s(out_5[2]));
  additionneur_complet2 additionneur_complet2_3 (
    .a(A[1]), .b(B[1]), .rin(additionneur_complet2_4_rout), .rout(additionneur_complet2_3_rout), .s(out_5[1]));
  additionneur_complet2 additionneur_complet2_4 (
    .a(A[0]), .b(B[0]), .rin(r0), .rout(additionneur_complet2_4_rout), .s(out_5[0]));
endmodule

module addition_affichage (
  input  [3:0] A,
  input  [3:0] B,
  input  r0,
  output r4,
  output [3:0] out_5
);

  Hex_Digit_Display hex_digit_display_1 (.value(A));  // open: dp
  Hex_Digit_Display hex_digit_display_2 (.value(B));  // open: dp
  additionneur4bits additionneur4bits_1 (.A(A), .B(B), .r0(r0), .r4(r4), .out_5(out_5));
  Hex_Digit_Display hex_digit_display_3 (.value(out_5));  // open: dp
endmodule

module additionneur_soustracteur (
  input  [3:0] A,
  input  [3:0] B,
  input  C,
  output R,
  output [3:0] S
);

  wire [3:0] xor_1_out;

  Hex_Digit_Display hex_digit_display_1 (.value(A));  // open: dp
  Hex_Digit_Display hex_digit_display_2 (.value(B));  // open: dp
  assign xor_1_out = B ^ {4{C}};  // XOR_Gate xor_1, 4 bits wide
  additionneur4bits additionneur4bits_1 (.A(A), .B(xor_1_out), .r0(C), .r4(R), .out_5(S));
  Hex_Digit_Display hex_digit_display_3 (.value(S));  // open: dp
endmodule

module add_sous_affichage (
  input  [3:0] A,
  input  [3:0] B,
  input  C,
  output r4,
  output [3:0] out_5
);

  Hex_Digit_Display hex_digit_display_1 (.value(A));  // open: dp
  Hex_Digit_Display hex_digit_display_2 (.value(B));  // open: dp
  additionneur_soustracteur additionneur_soustracteur_1 (.A(A), .B(B), .C(C), .R(r4), .S(out_5));
  Hex_Digit_Display hex_digit_display_3 (.value(out_5));  // open: dp
endmodule

module ByteToBCD (
  input  [7:0] E,
  output [3:0] C,
  output [3:0] D,
  output [3:0] U
);

  wire [7:0] divider_1_out;
  wire [7:4] divider_1_rem, divider_2_out, divider_2_rem;

  Divider divider_1 (.a(E), .b(8'ha), .out(divider_1_out), .rem({divider_1_rem, U}));  // open: upper
  Divider divider_2 (.a(divider_1_out), .b(8'ha), .out({divider_2_out, C}), .rem({divider_2_rem, D}));  // open: upper
endmodule

module add_sous_8bits (
  input  [7:0] in_1,
  input  [7:0] in_2,
  input  in_3,
  output [7:0] out_4
);

  wire additionneur4bits_2_r4;
  wire [3:0] bytetobcd_1_c, bytetobcd_1_d, bytetobcd_1_u, bytetobcd_2_c, bytetobcd_2_d, bytetobcd_2_u,
       bytetobcd_3_c, bytetobcd_3_d, bytetobcd_3_u;
  wire [7:0] xor_1_out;

  assign xor_1_out = in_2 ^ {8{in_3}};  // XOR_Gate xor_1, 8 bits wide
  ByteToBCD bytetobcd_1 (.E(in_1), .C(bytetobcd_1_c), .D(bytetobcd_1_d), .U(bytetobcd_1_u));
  ByteToBCD bytetobcd_2 (.E(in_2), .C(bytetobcd_2_c), .D(bytetobcd_2_d), .U(bytetobcd_2_u));
  additionneur4bits additionneur4bits_1 (
    .A(in_1[7:4]), .B(xor_1_out[7:4]), .r0(additionneur4bits_2_r4), .out_5(out_4[7:4]));  // open: r4
  additionneur4bits additionneur4bits_2 (
    .A(in_1[3:0]), .B(xor_1_out[3:0]), .r0(in_3), .r4(additionneur4bits_2_r4), .out_5(out_4[3:0]));
  Hex_Digit_Display hex_digit_display_1 (.value(bytetobcd_1_c));  // open: dp
  Hex_Digit_Display hex_digit_display_2 (.value(bytetobcd_1_d));  // open: dp
  Hex_Digit_Display hex_digit_display_3 (.value(bytetobcd_2_c));  // open: dp
  Hex_Digit_Display hex_digit_display_4 (.value(bytetobcd_2_d));  // open: dp
  Hex_Digit_Display hex_digit_display_5 (.value(bytetobcd_1_u));  // open: dp
  Hex_Digit_Display hex_digit_display_6 (.value(bytetobcd_2_u));  // open: dp
  ByteToBCD bytetobcd_3 (.E(out_4), .C(bytetobcd_3_c), .D(bytetobcd_3_d), .U(bytetobcd_3_u));
  Hex_Digit_Display hex_digit_display_7 (.value(bytetobcd_3_c));  // open: dp
  Hex_Digit_Display hex_digit_display_8 (.value(bytetobcd_3_d));  // open: dp
  Hex_Digit_Display hex_digit_display_9 (.value(bytetobcd_3_u));  // open: dp
endmodule
