// Logisim project Aff7seg.circ as structural Verilog: 3 circuits, main circuit aff7dec
module main (
  input  [3:0] E
);

  wire aff7dec_1_a, aff7dec_1_b, aff7dec_1_c, aff7dec_1_d, aff7dec_1_e, aff7dec_1_f, aff7dec_1_g;

  aff7dec aff7dec_1 (
    .i(E), .a(aff7dec_1_a), .b(aff7dec_1_b), .c(aff7dec_1_c), .d(aff7dec_1_d), .e(aff7dec_1_e),
    .f(aff7dec_1_f), .g(aff7dec_1_g));
  _7_Segment_Display u_7_segment_display_1 (
    .g(aff7dec_1_g), .f(aff7dec_1_f), .a(aff7dec_1_a), .b(aff7dec_1_b), .e(aff7dec_1_e), .d(aff7dec_1_d),
    .c(aff7dec_1_c));  // open: dp
endmodule

module aff7 (
  input  [3:0] i,
  output a,
  output b,
  output c,
  output d,
  output e,
  output f,
  output g
);

  wire and_1_out, and_2_out, and_3_out, and_4_out, and_5_out, and_6_out, and_7_out, and_8_out, and_9_out,
       and_10_out, and_11_out, and_12_out, and_13_out, and_14_out, and_15_out, and_16_out, and_17_out,
       and_18_out, and_19_out, and_20_out, and_21_out, and_22_out, and_23_out, and_24_out, and_25_out,
       and_26_out, and_27_out, and_28_out, and_29_out, and_30_out, and_31_out, and_32_out, and_33_out,
       and_34_out, and_35_out, and_36_out, not_1_out, not_2_out, not_3_out, not_4_out;

  not not_1 (not_1_out, i[3]);
  not not_2 (not_2_out, i[2]);
  not not_3 (not_3_out, i[1]);
  not not_4 (not_4_out, i[0]);
  and and_1 (and_1_out, not_2_out, not_4_out);
  and and_2 (and_2_out, not_1_out, i[1]);
  and and_3 (and_3_out, not_1_out, i[2], i[0]);
  and and_4 (and_4_out, i[2], i[1]);
  and and_5 (and_5_out, i[3], not_2_out, not_3_out);
  and and_6 (and_6_out, i[3], not_4_out);
  and and_7 (and_7_out, not_1_out, not_2_out);
  and and_8 (and_8_out, not_1_out, not_3_out, not_4_out);
  and and_9 (and_9_out, not_2_out, not_4_out);
  and and_10 (and_10_out, not_1_out, i[1], i[0]);
  and and_11 (and_11_out, i[3], not_3_out, i[0]);
  and and_12 (and_12_out, not_1_out, not_3_out);
  and and_13 (and_13_out, not_1_out, i[0]);
  and and_14 (and_14_out, not_3_out, i[0]);
  and and_15 (and_15_out, not_1_out, i[2]);
  and and_16 (and_16_out, i[3], not_2_out);
  and and_17 (and_17_out, not_1_out, not_2_out, not_4_out);
  and and_18 (and_18_out, not_1_out, i[1], not_4_out);
  and and_19 (and_19_out, not_2_out, i[1], i[0]);
  and and_20 (and_20_out, i[2], not_3_out, i[0]);
  and and_21 (and_21_out, i[3], not_3_out);
  and and_22 (and_22_out, i[3], i[2], not_4_out);
  and and_23 (and_23_out, not_2_out, not_4_out);
  and and_24 (and_24_out, i[1], not_4_out);
  and and_25 (and_25_out, i[3], i[1]);
  and and_26 (and_26_out, i[3], i[2]);
  and and_27 (and_27_out, not_3_out, not_4_out);
  and and_28 (and_28_out, not_1_out, i[2], not_3_out);
  and and_29 (and_29_out, i[2], not_4_out);
  and and_30 (and_30_out, i[3], not_2_out);
  and and_31 (and_31_out, i[3], i[1]);
  and and_32 (and_32_out, not_2_out, i[1]);
  and and_33 (and_33_out, i[1], not_4_out);
  and and_34 (and_34_out, not_1_out, i[2], not_3_out);
  and and_35 (and_35_out, i[3], not_2_out);
  and and_36 (and_36_out, i[3], i[0]);
  or or_1 (a, and_1_out, and_2_out, and_3_out, and_4_out, and_5_out, and_6_out);
  or or_2 (b, and_7_out, and_8_out, and_9_out, and_10_out, and_11_out);
  or or_3 (c, and_12_out, and_13_out, and_14_out, and_15_out, and_16_out);
  or or_4 (d, and_17_out, and_18_out, and_19_out, and_20_out, and_21_out, and_22_out);
  or or_5 (e, and_23_out, and_24_out, and_25_out, and_26_out);
  or or_6 (f, and_27_out, and_28_out, and_29_out, and_30_out, and_31_out);
  or or_7 (g, and_32_out, and_33_out, and_34_out, and_35_out, and_36_out);
endmodule

module aff7dec (
  input  [3:0] i,
  output a,
  output b,
  output c,
  output d,
  output e,
  output f,
  output g
);

  wire and_1_out, and_2_out, and_3_out, and_4_out, and_5_out, and_6_out, and_7_out, and_8_out, and_9_out,
       and_10_out, and_11_out, and_12_out, and_13_out, and_14_out, and_15_out, and_16_out, and_17_out,
       not_1_out, not_2_out, not_3_out, not_4_out;

  not not_1 (not_1_out, i[3]);
  not not_2 (not_2_out, i[2]);
  not not_3 (not_3_out, i[1]);
  not not_4 (not_4_out, i[0]);
  and and_1 (and_1_out, not_2_out, not_4_out);
  and and_2 (and_2_out, i[2], i[0]);
  and and_3 (and_3_out, not_3_out, not_4_out);
  or or_1 (b, not_2_out, and_3_out, and_4_out);
  and and_4 (and_4_out, i[1], i[0]);
  or or_2 (c, not_3_out, i[0], i[2], i[3]);
  and and_5 (and_5_out, not_2_out, not_3_out, not_4_out);
  and and_6 (and_6_out, not_1_out, not_2_out, i[1]);
  and and_7 (and_7_out, not_1_out, i[1], not_4_out);
  and and_8 (and_8_out, i[2], not_3_out, i[0]);
  and and_9 (and_9_out, i[3], not_3_out);
  and and_10 (and_10_out, not_2_out, not_4_out);
  or or_3 (e, and_10_out, and_11_out);
  and and_11 (and_11_out, i[1], not_4_out);
  and and_12 (and_12_out, not_3_out, not_4_out);
  and and_13 (and_13_out, i[2], not_3_out);
  and and_14 (and_14_out, i[2], not_4_out);
  and and_15 (and_15_out, not_2_out, i[1]);
  and and_16 (and_16_out, i[2], not_3_out);
  and and_17 (and_17_out, i[2], not_4_out);
  or or_4 (a, and_1_out, i[1], and_2_out, i[3]);
  or or_5 (d, and_5_out, and_6_out, and_7_out, and_8_out, and_9_out);
  or or_6 (f, and_12_out, and_13_out, and_14_out, i[3]);
  or or_7 (g, and_15_out, and_16_out, and_17_out, i[3]);
endmodule
