// Logisim project ByteToBCD.circ as structural Verilog: 1 circuit, main circuit ByteToBCD
module ByteToBCD (
  input  [7:0] E,
  output [3:0] C,
  output [3:0] D,
  output [3:0] U
);

  wire [7:0] divider_1_out;
  wire [7:4] divider_1_rem, divider_2_out, divider_2_rem;

  Divider divider_1 (.a(E), .b(8'ha), .out(divider_1_out), .rem({divider_1_rem, U}));  // open: upper
  Divider divider_2 (.a(divider_1_out), .b(8'ha), .out({divider_2_out, C}), .rem({divider_2_rem, D}));  // open: upper
endmodule
