// Logisim project FF.circ as structural Verilog: 7 circuits, main circuit RS
module RS (
  input  S,
  input  R,
  output Q,
  output NOT_Q
);

  wire not_1_out, not_2_out;

  not not_1 (not_1_out, S);
  not not_2 (not_2_out, R);
  nand nand_1 (Q, not_1_out, NOT_Q);
  nand nand_2 (NOT_Q, Q, not_2_out);
endmodule

module RSClock (
  input  S,
  input  H,
  input  R,
  output Q,
  output NOT_Q
);

  wire nand_1_out, nand_2_out;

  nand nand_1 (nand_1_out, S, H);
  nand nand_2 (nand_2_out, H, R);
  nand nand_3 (Q, nand_1_out, NOT_Q);
  nand nand_4 (NOT_Q, Q, nand_2_out);
endmodule

module JK (
  input  J,
  input  H,
  input  K,
  output Q,
  output Not_Q
);

  wire and_1_out, and_2_out;

  and and_1 (and_1_out, Not_Q, J);
  and and_2 (and_2_out, K, Q);
  RSClock rsclock_1 (.S(and_1_out), .H(H), .R(and_2_out), .Q(Q), .NOT_Q(Not_Q));
endmodule

module JKAsync (
  input  Pr,
  input  J,
  input  H,
  input  K,
  input  Cr,
  output Q,
  output NOT_Q
);

  wire nand_1_out, nand_2_out;

  nand nand_1 (nand_1_out, J, H, NOT_Q);
  nand nand_2 (nand_2_out, Q, H, K);
  nand nand_3 (Q, Pr, nand_1_out, NOT_Q);
  nand nand_4 (NOT_Q, Q, nand_2_out, Cr);
endmodule

module JKMaster (
  input  Pr,
  input  J,
  input  H,
  input  K,
  input  Cr,
  output Q,
  output NOT_Q
);

  wire nand_1_out, nand_2_out, nand_3_out, nand_4_out, nand_5_out, nand_6_out, not_1_out;

  nand nand_1 (nand_1_out, NOT_Q, J, H);
  nand nand_2 (nand_2_out, H, K, Q);
  nand nand_3 (nand_3_out, Pr, nand_1_out, nand_4_out);
  nand nand_4 (nand_4_out, nand_3_out, nand_2_out, Cr);
  not not_1 (not_1_out, H);
  nand nand_5 (nand_5_out, nand_3_out, not_1_out);
  nand nand_6 (nand_6_out, not_1_out, nand_4_out);
  nand nand_7 (Q, nand_5_out, NOT_Q);
  nand nand_8 (NOT_Q, Q, nand_6_out);
endmodule

module D (
  input  Pr,
  input  in_2,
  input  H,
  input  Cr,
  output Q
);

  wire not_1_out;

  JKMaster jkmaster_1 (.J(in_2), .H(H), .K(not_1_out), .Pr(Pr), .Cr(Cr), .Q(Q));  // open: NOT_Q
  not not_1 (not_1_out, in_2);
endmodule

module T (
  input  Pr,
  input  in_2,
  input  H,
  input  Cr,
  output Q
);

  JKMaster jkmaster_1 (.J(in_2), .H(H), .K(in_2), .Pr(Pr), .Cr(Cr), .Q(Q));  // open: NOT_Q
endmodule
