// Logisim project HighLevel.circ as structural Verilog: 7 circuits, main circuit decodeur_instruction
module decodeur_instruction (
  input  [1:0] code,
  output [7:0] add
);


  assign add = {4'b0000, code, 2'b00};
endmodule

module UC (
  input  [1:0] in_1
);

  wire button_1_out, clock_1_out, not_1_out;
  wire [7:0] counter_1_q, decodeur_instruction_1_add, rom_1_data;

  Clock clock_1 (.out(clock_1_out));
  decodeur_instruction decodeur_instruction_1 (.code(in_1), .add(decodeur_instruction_1_add));
  Counter counter_1 (
    .load(button_1_out), .count(not_1_out), .clk(clock_1_out), .D(decodeur_instruction_1_add), .Q(counter_1_q));  // open: clr, up, carry
  Button button_1 (.out(button_1_out));
  not not_1 (not_1_out, rom_1_data[7]);
  ROM rom_1 (.addr(counter_1_q), .data(rom_1_data));

  // Notes on the sheet:
  //   contents of rom_1 (hex, n*v repeats v):
  //   3 4 80 0 1 8 10 80 0 0 0 80 0 80
endmodule

module sequenceur (
  input  UpDown,
  input  EN,
  input  [7:0] E,
  output [7:0] S
);

  wire clock_1_out, Load_out, RAZ_out;

  Button RAZ (.out(RAZ_out));
  Button Load (.out(Load_out));
  Clock clock_1 (.out(clock_1_out));
  Counter counter_1 (
    .clr(RAZ_out), .load(Load_out), .up(UpDown), .count(EN), .clk(clock_1_out), .D(E), .Q(S));  // open: carry
endmodule

module execution (
  input  [17:0] in_1,
  output [7:0] out_2
);

  wire button_1_out, clock_1_out, not_1_out;
  wire [7:0] counter_1_q, decodeur_instruction_1_add, ram_1_dout, register_1_q, register_2_q, rom_1_data;

  Clock clock_1 (.out(clock_1_out));
  decodeur_instruction decodeur_instruction_1 (.code(in_1[17:16]), .add(decodeur_instruction_1_add));
  Counter counter_1 (
    .load(button_1_out), .count(not_1_out), .clk(clock_1_out), .D(decodeur_instruction_1_add), .Q(counter_1_q));  // open: clr, up, carry
  Button button_1 (.out(button_1_out));
  not not_1 (not_1_out, rom_1_data[7]);
  ROM rom_1 (.addr(counter_1_q), .data(rom_1_data));
  Register register_1 (.D(in_1[15:8]), .en(rom_1_data[0]), .clk(clock_1_out), .Q(register_1_q));  // open: clr
  Register register_2 (.D(in_1[7:0]), .en(rom_1_data[1]), .clk(clock_1_out), .Q(register_2_q));  // open: clr
  RAM ram_1 (
    .addr(register_1_q), .we(rom_1_data[2]), .oe(rom_1_data[3]), .clk(clock_1_out), .din(register_2_q),
    .dout(ram_1_dout));
  Register register_3 (.D(ram_1_dout), .en(rom_1_data[4]), .clk(clock_1_out), .Q(out_2));  // open: clr

  // Notes on the sheet:
  //   contents of rom_1 (hex, n*v repeats v):
  //   3 4 80 0 1 8 10 80
endmodule

module registre (
  input  [7:0] in_1,
  input  in_2,
  output [7:0] out_3
);

  wire clock_1_out;

  Clock clock_1 (.out(clock_1_out));
  Register register_1 (.D(in_1), .en(in_2), .clk(clock_1_out), .Q(out_3));  // open: clr
endmodule

module test_ROM (
  input  [7:0] in_1,
  output [7:0] out_2
);

  ROM rom_1 (.addr(in_1), .data(out_2));

  // Notes on the sheet:
  //   contents of rom_1 (hex, n*v repeats v):
  //   0 14 a5 b2 75 bd ea 4e 2e a5 56 43 26 76 32 56 2e ee bd dd d5 3b cc ca 7b fa be 3d 18 89 43 32
endmodule

module test_RAM (
  input  [7:0] Adresse,
  input  W,
  input  R,
  input  [7:0] E,
  output [7:0] S
);

  wire clock_1_out;

  Clock clock_1 (.out(clock_1_out));
  RAM ram_1 (.addr(Adresse), .we(W), .oe(R), .clk(clock_1_out), .din(E), .dout(S));
endmodule
