// Logisim project Memoire.circ as structural Verilog: 7 circuits, main circuit Reg1bit
module Reg1bit (
  input  E,
  input  W,
  input  R,
  input  EN,
  output out_5
);

  wire and_1_out, d_ff_1_q;

  D_Flip_Flop d_ff_1 (.D(E), .clk(and_1_out), .Q(d_ff_1_q));  // open: Qn, preset, reset
  and and_1 (and_1_out, W, EN);
  and and_2 (out_5, d_ff_1_q, R, EN);
endmodule

module Reg4bits (
  input  [3:0] E,
  input  W,
  input  R,
  input  EN,
  output [3:0] S
);

  Reg1bit reg1bit_1 (.E(E[0]), .W(W), .R(R), .EN(EN), .out_5(S[0]));
  Reg1bit reg1bit_2 (.E(E[1]), .W(W), .R(R), .EN(EN), .out_5(S[1]));
  Reg1bit reg1bit_3 (.E(E[2]), .W(W), .R(R), .EN(EN), .out_5(S[2]));
  Reg1bit reg1bit_4 (.E(E[3]), .W(W), .R(R), .EN(EN), .out_5(S[3]));
endmodule

module Memoire8x4bits (
  input  [3:0] E,
  input  W,
  input  R,
  input  [2:0] A,
  output [3:0] S
);

  wire [3:0] reg4bits_1_s, reg4bits_2_s, reg4bits_3_s, reg4bits_4_s, reg4bits_5_s, reg4bits_6_s,
       reg4bits_7_s, reg4bits_8_s;
  wire [7:0] decodeur3_1_s;

  decodeur3 decodeur3_1 (.E(A), .S(decodeur3_1_s));
  Reg4bits reg4bits_1 (.E(E), .W(W), .R(R), .EN(decodeur3_1_s[0]), .S(reg4bits_1_s));
  Reg4bits reg4bits_2 (.E(E), .W(W), .R(R), .EN(decodeur3_1_s[1]), .S(reg4bits_2_s));
  Reg4bits reg4bits_3 (.E(E), .W(W), .R(R), .EN(decodeur3_1_s[2]), .S(reg4bits_3_s));
  Reg4bits reg4bits_4 (.E(E), .W(W), .R(R), .EN(decodeur3_1_s[3]), .S(reg4bits_4_s));
  Reg4bits reg4bits_5 (.E(E), .W(W), .R(R), .EN(decodeur3_1_s[4]), .S(reg4bits_5_s));
  Reg4bits reg4bits_6 (.E(E), .W(W), .R(R), .EN(decodeur3_1_s[5]), .S(reg4bits_6_s));
  Reg4bits reg4bits_7 (.E(E), .W(W), .R(R), .EN(decodeur3_1_s[6]), .S(reg4bits_7_s));
  Reg4bits reg4bits_8 (.E(E), .W(W), .R(R), .EN(decodeur3_1_s[7]), .S(reg4bits_8_s));
  assign S = reg4bits_1_s | reg4bits_2_s | reg4bits_3_s | reg4bits_4_s | reg4bits_5_s | reg4bits_6_s | reg4bits_7_s | reg4bits_8_s;  // OR_Gate or_1, 4 bits wide
endmodule

module decodeur3 (
  input  [2:0] E,
  output [7:0] S
);

  wire not_1_out, not_2_out, not_3_out;

  not not_1 (not_1_out, E[2]);
  not not_2 (not_2_out, E[1]);
  not not_3 (not_3_out, E[0]);
  and and_1 (S[7], E[2], E[1], E[0]);
  and and_2 (S[6], E[2], E[1], not_3_out);
  and and_3 (S[5], E[2], not_2_out, E[0]);
  and and_4 (S[4], E[2], not_2_out, not_3_out);
  and and_5 (S[3], not_1_out, E[1], E[0]);
  and and_6 (S[2], not_1_out, E[1], not_3_out);
  and and_7 (S[1], not_1_out, not_2_out, E[0]);
  and and_8 (S[0], not_1_out, not_2_out, not_3_out);
endmodule

module Memoire8x4bitsEN (
  input  [3:0] E,
  input  W,
  input  R,
  input  [2:0] A,
  input  EN,
  output [3:0] S
);

  wire [3:0] reg4bits_1_s, reg4bits_2_s, reg4bits_3_s, reg4bits_4_s, reg4bits_5_s, reg4bits_6_s,
       reg4bits_7_s, reg4bits_8_s;
  wire [7:0] and_1_out, decodeur3_1_s;

  decodeur3 decodeur3_1 (.E(A), .S(decodeur3_1_s));
  assign and_1_out = decodeur3_1_s & {8{EN}};  // AND_Gate and_1, 8 bits wide
  Reg4bits reg4bits_1 (.E(E), .W(W), .R(R), .EN(and_1_out[0]), .S(reg4bits_1_s));
  Reg4bits reg4bits_2 (.E(E), .W(W), .R(R), .EN(and_1_out[1]), .S(reg4bits_2_s));
  Reg4bits reg4bits_3 (.E(E), .W(W), .R(R), .EN(and_1_out[2]), .S(reg4bits_3_s));
  Reg4bits reg4bits_4 (.E(E), .W(W), .R(R), .EN(and_1_out[3]), .S(reg4bits_4_s));
  Reg4bits reg4bits_5 (.E(E), .W(W), .R(R), .EN(and_1_out[4]), .S(reg4bits_5_s));
  Reg4bits reg4bits_6 (.E(E), .W(W), .R(R), .EN(and_1_out[5]), .S(reg4bits_6_s));
  Reg4bits reg4bits_7 (.E(E), .W(W), .R(R), .EN(and_1_out[6]), .S(reg4bits_7_s));
  Reg4bits reg4bits_8 (.E(E), .W(W), .R(R), .EN(and_1_out[7]), .S(reg4bits_8_s));
  assign S = reg4bits_1_s | reg4bits_2_s | reg4bits_3_s | reg4bits_4_s | reg4bits_5_s | reg4bits_6_s | reg4bits_7_s | reg4bits_8_s;  // OR_Gate or_1, 4 bits wide
endmodule

module Memoire32x4bits (
  input  [3:0] E,
  input  W,
  input  R,
  input  [4:0] A,
  output [3:0] S
);

  wire [3:0] decodeur2_1_s, memoire8x4bitsen_1_s, memoire8x4bitsen_2_s, memoire8x4bitsen_3_s,
       memoire8x4bitsen_4_s;

  decodeur2 decodeur2_1 (.E(A[4:3]), .S(decodeur2_1_s));
  Memoire8x4bitsEN memoire8x4bitsen_1 (
    .E(E), .W(W), .R(R), .A(A[2:0]), .EN(decodeur2_1_s[0]), .S(memoire8x4bitsen_1_s));
  Memoire8x4bitsEN memoire8x4bitsen_2 (
    .E(E), .W(W), .R(R), .A(A[2:0]), .EN(decodeur2_1_s[1]), .S(memoire8x4bitsen_2_s));
  Memoire8x4bitsEN memoire8x4bitsen_3 (
    .E(E), .W(W), .R(R), .A(A[2:0]), .EN(decodeur2_1_s[2]), .S(memoire8x4bitsen_3_s));
  Memoire8x4bitsEN memoire8x4bitsen_4 (
    .E(E), .W(W), .R(R), .A(A[2:0]), .EN(decodeur2_1_s[3]), .S(memoire8x4bitsen_4_s));
  assign S = memoire8x4bitsen_1_s | memoire8x4bitsen_2_s | memoire8x4bitsen_3_s | memoire8x4bitsen_4_s;  // OR_Gate or_1, 4 bits wide
endmodule

module decodeur2 (
  input  [1:0] E,
  output [3:0] S
);

  wire not_1_out, not_2_out;

  not not_1 (not_1_out, E[1]);
  not not_2 (not_2_out, E[0]);
  and and_1 (S[3], E[1], E[0]);
  and and_2 (S[2], E[1], not_2_out);
  and and_3 (S[1], not_1_out, E[0]);
  and and_4 (S[0], not_1_out, not_2_out);
endmodule
