// Logisim project Plexer.circ as structural Verilog: 8 circuits, main circuit L_2coder
module L_2coder (
  input  e1,
  input  e0,
  output s0
);

  not not_1 (s0, e0);
endmodule

module L_4coder (
  input  e3,
  input  e2,
  input  e1,
  input  e0,
  output s1,
  output s0
);

  wire not_1_out, not_2_out, not_3_out, not_4_out;

  not not_1 (not_1_out, e1);
  and and_1 (s1, not_1_out, not_2_out);
  not not_2 (not_2_out, e0);
  not not_3 (not_3_out, e2);
  and and_2 (s0, not_3_out, not_4_out);
  not not_4 (not_4_out, e0);
endmodule

module L_2decoder (
  input  e0,
  output s1,
  output s0
);

  not not_1 (s0, e0);

  assign s1 = e0;
endmodule

module L_4decoder (
  input  e1,
  input  e0,
  output s3,
  output s2,
  output s1,
  output s0
);

  wire not_1_out, not_2_out, not_3_out, not_4_out;

  and and_1 (s3, e1, e0);
  not not_1 (not_1_out, e0);
  not not_2 (not_2_out, e1);
  not not_3 (not_3_out, e1);
  not not_4 (not_4_out, e0);
  and and_2 (s2, e1, not_1_out);
  and and_3 (s1, not_2_out, e0);
  and and_4 (s0, not_3_out, not_4_out);
endmodule

module L_2mux (
  input  e1,
  input  e0,
  input  a0,
  output s
);

  wire and_1_out, and_2_out, not_1_out;

  not not_1 (not_1_out, a0);
  and and_1 (and_1_out, e0, not_1_out);
  and and_2 (and_2_out, e1, a0);
  or or_1 (s, and_1_out, and_2_out);
endmodule

module L_4mux (
  input  e3,
  input  e2,
  input  e1,
  input  e0,
  input  a1,
  input  a0,
  output s
);

  wire and_1_out, and_2_out, and_3_out, and_4_out, not_1_out, not_2_out, not_3_out, not_4_out;

  not not_1 (not_1_out, a0);
  not not_2 (not_2_out, a1);
  not not_3 (not_3_out, a1);
  not not_4 (not_4_out, a0);
  and and_1 (and_1_out, not_1_out, not_2_out, e0);
  and and_2 (and_2_out, a0, not_3_out, e1);
  and and_3 (and_3_out, not_4_out, a1, e2);
  and and_4 (and_4_out, a0, a1, e3);
  or or_1 (s, and_1_out, and_2_out, and_3_out, and_4_out);
endmodule

module L_2demux (
  input  e,
  input  a0,
  output s1,
  output s0
);

  wire not_1_out;

  and and_1 (s1, e, a0);
  not not_1 (not_1_out, a0);
  and and_2 (s0, e, not_1_out);
endmodule

module L_4demux (
  input  e,
  input  a1,
  input  a0,
  output s3,
  output s2,
  output s1,
  output s0
);

  wire not_1_out, not_2_out, not_3_out, not_4_out;

  and and_1 (s3, e, a1, a0);
  not not_1 (not_1_out, a0);
  not not_2 (not_2_out, a1);
  not not_3 (not_3_out, a1);
  not not_4 (not_4_out, a0);
  and and_2 (s2, e, a1, not_1_out);
  and and_3 (s1, e, not_2_out, a0);
  and and_4 (s0, e, not_3_out, not_4_out);
endmodule
