// Logisim project Sequenceur.circ as structural Verilog: 4 circuits, main circuit asynchrone_0_5
module asynchrone_0_5 (
  output out_1,
  output out_2,
  output out_3
);

  wire and_1_out, clock_1_out, j_k_ff_1_qn, j_k_ff_2_qn, not_1_out;

  Clock clock_1 (.out(clock_1_out));
  not not_1 (not_1_out, clock_1_out);
  J_K_Flip_Flop j_k_ff_1 (
    .J(1'b1), .K(1'b1), .clk(not_1_out), .Q(out_1), .Qn(j_k_ff_1_qn), .reset(and_1_out));  // open: preset
  J_K_Flip_Flop j_k_ff_2 (
    .J(1'b1), .K(1'b1), .clk(j_k_ff_1_qn), .Q(out_2), .Qn(j_k_ff_2_qn), .reset(and_1_out));  // open: preset
  J_K_Flip_Flop j_k_ff_3 (.J(1'b1), .K(1'b1), .clk(j_k_ff_2_qn), .Q(out_3), .reset(and_1_out));  // open: Qn, preset
  and and_1 (and_1_out, out_3, out_2);
endmodule

module asynchrone_0_7 (
  output out_1,
  output out_2,
  output out_3
);

  wire clock_1_out, j_k_ff_1_qn, j_k_ff_2_qn, not_1_out;

  Clock clock_1 (.out(clock_1_out));
  not not_1 (not_1_out, clock_1_out);
  J_K_Flip_Flop j_k_ff_1 (.J(1'b1), .K(1'b1), .clk(not_1_out), .Q(out_1), .Qn(j_k_ff_1_qn));  // open: preset, reset
  J_K_Flip_Flop j_k_ff_2 (.J(1'b1), .K(1'b1), .clk(j_k_ff_1_qn), .Q(out_2), .Qn(j_k_ff_2_qn));  // open: preset, reset
  J_K_Flip_Flop j_k_ff_3 (.J(1'b1), .K(1'b1), .clk(j_k_ff_2_qn), .Q(out_3));  // open: Qn, preset, reset
endmodule

module synchrone_0_5 (
  output [2:0] out_1
);

  wire clock_1_out;
  wire [2:0] combinatoire_1_s;

  Clock clock_1 (.out(clock_1_out));
  D_Flip_Flop d_ff_1 (.D(combinatoire_1_s[0]), .clk(clock_1_out), .Q(out_1[0]));  // open: Qn, preset, reset
  D_Flip_Flop d_ff_2 (.D(combinatoire_1_s[1]), .clk(clock_1_out), .Q(out_1[1]));  // open: Qn, preset, reset
  D_Flip_Flop d_ff_3 (.D(combinatoire_1_s[2]), .clk(clock_1_out), .Q(out_1[2]));  // open: Qn, preset, reset
  combinatoire combinatoire_1 (.E(out_1), .S(combinatoire_1_s));
endmodule

module combinatoire (
  input  [2:0] E,
  output [2:0] S
);

  wire and_1_out, and_2_out, and_3_out, and_4_out, not_1_out, not_2_out;

  not not_1 (not_1_out, E[2]);
  not not_2 (not_2_out, E[1]);
  not not_3 (S[0], E[0]);
  and and_1 (and_1_out, E[1], E[0]);
  and and_2 (and_2_out, E[2], S[0]);
  and and_3 (and_3_out, not_1_out, not_2_out, E[0]);
  and and_4 (and_4_out, E[1], S[0]);
  or or_1 (S[2], and_1_out, and_2_out);
  or or_2 (S[1], and_3_out, and_4_out);
endmodule
