// Logisim project Sequentiel.circ as structural Verilog: 9 circuits, main circuit Horloge_1
module Horloge_1 (
  output S
);

  Clock #(.highDuration(2)) H (.out(S));
endmodule

module Horloge_2 (
  output out_1,
  output out_2,
  output out_3,
  output out_4
);

  wire aff7_1_a, aff7_1_b, aff7_1_c, aff7_1_d, aff7_1_e, aff7_1_f, aff7_1_g;

  Clock H0 (.out(out_1));
  Clock #(.highDuration(2), .lowDuration(2)) H1 (.out(out_2));
  Clock #(.highDuration(4), .lowDuration(4)) H2 (.out(out_3));
  Clock #(.highDuration(8), .lowDuration(8)) H3 (.out(out_4));
  aff7 aff7_1 (
    .i({out_4, out_3, out_2, out_1}), .a(aff7_1_a), .b(aff7_1_b), .c(aff7_1_c), .d(aff7_1_d), .e(aff7_1_e),
    .f(aff7_1_f), .g(aff7_1_g));
  _7_Segment_Display u_7_segment_display_1 (
    .g(aff7_1_g), .f(aff7_1_f), .a(aff7_1_a), .b(aff7_1_b), .e(aff7_1_e), .d(aff7_1_d), .c(aff7_1_c));  // open: dp
endmodule

module aff7 (
  input  [3:0] i,
  output a,
  output b,
  output c,
  output d,
  output e,
  output f,
  output g
);

  wire and_1_out, and_2_out, and_3_out, and_4_out, and_5_out, and_6_out, and_7_out, and_8_out, and_9_out,
       and_10_out, and_11_out, and_12_out, and_13_out, and_14_out, and_15_out, and_16_out, and_17_out,
       and_18_out, and_19_out, and_20_out, and_21_out, and_22_out, and_23_out, and_24_out, and_25_out,
       and_26_out, and_27_out, and_28_out, and_29_out, and_30_out, and_31_out, and_32_out, and_33_out,
       and_34_out, and_35_out, and_36_out, not_1_out, not_2_out, not_3_out, not_4_out;

  not not_1 (not_1_out, i[3]);
  not not_2 (not_2_out, i[2]);
  not not_3 (not_3_out, i[1]);
  not not_4 (not_4_out, i[0]);
  and and_1 (and_1_out, not_2_out, not_4_out);
  and and_2 (and_2_out, not_1_out, i[1]);
  and and_3 (and_3_out, not_1_out, i[2], i[0]);
  and and_4 (and_4_out, i[2], i[1]);
  and and_5 (and_5_out, i[3], not_2_out, not_3_out);
  and and_6 (and_6_out, i[3], not_4_out);
  and and_7 (and_7_out, not_1_out, not_2_out);
  and and_8 (and_8_out, not_1_out, not_3_out, not_4_out);
  and and_9 (and_9_out, not_2_out, not_4_out);
  and and_10 (and_10_out, not_1_out, i[1], i[0]);
  and and_11 (and_11_out, i[3], not_3_out, i[0]);
  and and_12 (and_12_out, not_1_out, not_3_out);
  and and_13 (and_13_out, not_1_out, i[0]);
  and and_14 (and_14_out, not_3_out, i[0]);
  and and_15 (and_15_out, not_1_out, i[2]);
  and and_16 (and_16_out, i[3], not_2_out);
  and and_17 (and_17_out, not_1_out, not_2_out, not_4_out);
  and and_18 (and_18_out, not_1_out, i[1], not_4_out);
  and and_19 (and_19_out, not_2_out, i[1], i[0]);
  and and_20 (and_20_out, i[2], not_3_out, i[0]);
  and and_21 (and_21_out, i[3], not_3_out);
  and and_22 (and_22_out, i[3], i[2], not_4_out);
  and and_23 (and_23_out, not_2_out, not_4_out);
  and and_24 (and_24_out, i[1], not_4_out);
  and and_25 (and_25_out, i[3], i[1]);
  and and_26 (and_26_out, i[3], i[2]);
  and and_27 (and_27_out, not_3_out, not_4_out);
  and and_28 (and_28_out, not_1_out, i[2], not_3_out);
  and and_29 (and_29_out, i[2], not_4_out);
  and and_30 (and_30_out, i[3], not_2_out);
  and and_31 (and_31_out, i[3], i[1]);
  and and_32 (and_32_out, not_2_out, i[1]);
  and and_33 (and_33_out, i[1], not_4_out);
  and and_34 (and_34_out, not_1_out, i[2], not_3_out);
  and and_35 (and_35_out, i[3], not_2_out);
  and and_36 (and_36_out, i[3], i[0]);
  or or_1 (a, and_1_out, and_2_out, and_3_out, and_4_out, and_5_out, and_6_out);
  or or_2 (b, and_7_out, and_8_out, and_9_out, and_10_out, and_11_out);
  or or_3 (c, and_12_out, and_13_out, and_14_out, and_15_out, and_16_out);
  or or_4 (d, and_17_out, and_18_out, and_19_out, and_20_out, and_21_out, and_22_out);
  or or_5 (e, and_23_out, and_24_out, and_25_out, and_26_out);
  or or_6 (f, and_27_out, and_28_out, and_29_out, and_30_out, and_31_out);
  or or_7 (g, and_32_out, and_33_out, and_34_out, and_35_out, and_36_out);
endmodule

module Bascules (
  input  S_asynch,
  input  R_asynch,
  input  S,
  input  R,
  input  J,
  input  K,
  input  D,
  input  T,
  output Q_RS,
  output Q_JK,
  output Q_D,
  output Q_T
);

  wire H_out;

  Clock H (.out(H_out));
  S_R_Flip_Flop s_r_ff_1 (.S(S), .R(R), .clk(H_out), .Q(Q_RS), .reset(R_asynch), .preset(S_asynch));  // open: Qn
  J_K_Flip_Flop j_k_ff_1 (.J(J), .K(K), .clk(H_out), .Q(Q_JK), .preset(S_asynch), .reset(R_asynch));  // open: Qn
  D_Flip_Flop d_ff_1 (.D(D), .clk(H_out), .Q(Q_D), .preset(S_asynch), .reset(R_asynch));  // open: Qn
  T_Flip_Flop t_ff_1 (.T(T), .clk(H_out), .Q(Q_T), .reset(R_asynch), .preset(S_asynch));  // open: Qn
endmodule

module Shift_left (
  input  E,
  output [3:0] S
);

  wire clock_1_out;

  Clock clock_1 (.out(clock_1_out));
  D_Flip_Flop d_ff_1 (.D(E), .clk(clock_1_out), .Q(S[0]));  // open: Qn, preset, reset
  D_Flip_Flop d_ff_2 (.D(S[0]), .clk(clock_1_out), .Q(S[1]));  // open: Qn, preset, reset
  D_Flip_Flop d_ff_3 (.D(S[1]), .clk(clock_1_out), .Q(S[2]));  // open: Qn, preset, reset
  D_Flip_Flop d_ff_4 (.D(S[2]), .clk(clock_1_out), .Q(S[3]));  // open: Qn, preset, reset
endmodule

module Shift_right (
  input  E,
  output [3:0] S
);

  wire clock_1_out;

  Clock clock_1 (.out(clock_1_out));
  D_Flip_Flop d_ff_1 (.D(E), .clk(clock_1_out), .Q(S[3]));  // open: Qn, preset, reset
  D_Flip_Flop d_ff_2 (.D(S[3]), .clk(clock_1_out), .Q(S[2]));  // open: Qn, preset, reset
  D_Flip_Flop d_ff_3 (.D(S[2]), .clk(clock_1_out), .Q(S[1]));  // open: Qn, preset, reset
  D_Flip_Flop d_ff_4 (.D(S[1]), .clk(clock_1_out), .Q(S[0]));  // open: Qn, preset, reset
endmodule

module Shift_left_right (
  input  LR,
  input  E,
  output [3:0] S
);

  wire clock_1_out;
  wire [3:0] d_ff_1_q;

  Clock clock_1 (.out(clock_1_out));
  D_Flip_Flop d_ff_1 (.D(E), .clk(clock_1_out), .Q(d_ff_1_q[3]));  // open: Qn, preset, reset
  D_Flip_Flop d_ff_2 (.D(d_ff_1_q[3]), .clk(clock_1_out), .Q(d_ff_1_q[2]));  // open: Qn, preset, reset
  D_Flip_Flop d_ff_3 (.D(d_ff_1_q[2]), .clk(clock_1_out), .Q(d_ff_1_q[1]));  // open: Qn, preset, reset
  D_Flip_Flop d_ff_4 (.D(d_ff_1_q[1]), .clk(clock_1_out), .Q(d_ff_1_q[0]));  // open: Qn, preset, reset
  Multiplexer #(.width(4)) multiplexer_1 (
    .in0(d_ff_1_q), .in1({d_ff_1_q[0], d_ff_1_q[1], d_ff_1_q[2], d_ff_1_q[3]}), .out(S), .sel(LR));
endmodule

module Rotation (
  input  Input_1,
  input  Input_0,
  output [3:0] S
);

  wire and_1_out, and_2_out, and_3_out, clock_1_out, not_1_out, or_1_out;

  not not_1 (not_1_out, Input_0);
  and and_1 (and_1_out, Input_1, S[3]);
  and and_2 (and_2_out, S[3], not_1_out);
  and and_3 (and_3_out, Input_1, not_1_out);
  Clock clock_1 (.out(clock_1_out));
  D_Flip_Flop d_ff_1 (.D(or_1_out), .clk(clock_1_out), .Q(S[0]));  // open: Qn, preset, reset
  or or_1 (or_1_out, and_1_out, and_2_out, and_3_out);
  D_Flip_Flop d_ff_2 (.D(S[0]), .clk(clock_1_out), .Q(S[1]));  // open: Qn, preset, reset
  D_Flip_Flop d_ff_3 (.D(S[1]), .clk(clock_1_out), .Q(S[2]));  // open: Qn, preset, reset
  D_Flip_Flop d_ff_4 (.D(S[2]), .clk(clock_1_out), .Q(S[3]));  // open: Qn, preset, reset
endmodule

module Shift_left_right_2 (
  input  E,
  input  LR,
  output [3:0] S
);

  wire H_out, multiplexer_1_out, multiplexer_2_out, multiplexer_3_out, multiplexer_4_out;

  Clock H (.out(H_out));
  D_Flip_Flop d_ff_1 (.D(multiplexer_1_out), .clk(H_out), .Q(S[0]));  // open: Qn, preset, reset
  Multiplexer multiplexer_1 (.in0(E), .in1(S[1]), .out(multiplexer_1_out), .sel(LR));
  D_Flip_Flop d_ff_2 (.D(multiplexer_2_out), .clk(H_out), .Q(S[1]));  // open: Qn, preset, reset
  Multiplexer multiplexer_2 (.in0(S[0]), .in1(S[2]), .out(multiplexer_2_out), .sel(LR));
  D_Flip_Flop d_ff_3 (.D(multiplexer_3_out), .clk(H_out), .Q(S[2]));  // open: Qn, preset, reset
  Multiplexer multiplexer_3 (.in0(S[1]), .in1(S[3]), .out(multiplexer_3_out), .sel(LR));
  D_Flip_Flop d_ff_4 (.D(multiplexer_4_out), .clk(H_out), .Q(S[3]));  // open: Qn, preset, reset
  Multiplexer multiplexer_4 (.in0(S[2]), .in1(E), .out(multiplexer_4_out), .sel(LR));
endmodule
